# Fritzing sketch grove-lcd-rgb (saved by Fritzing 0.9.3b)

parts:
  Grove2 = Grove OLED 128x96
  Raspberry_Pi1 = Raspberry Pi 2
  Composant1 = Logic Level Converter

nets:
  GND: Grove2.GND, Raspberry_Pi1.GND, Composant1.GND
  VCC: Grove2.VCC, Raspberry_Pi1.5V
  N1: Grove2.SDA, Composant1.RX2_HV
  N2: Grove2.SCL, Composant1.TX2_HV
  N3: Raspberry_Pi1.GPIO2, Composant1.RX2_LV
  N4: Raspberry_Pi1.GPIO3, Composant1.TX2_LV
