# Fritzing sketch rgb-lcd-rpi-mini (saved by Fritzing 0.9.3b)
breadboards: 1

parts:
  Raspberry_Pi1 = Raspberry Pi 2
  LCD1 = Adafruit Positive RGB 2x16 LCD
  R1 = TRIMPOT [package=3386u]

nets:
  N1: Raspberry_Pi1.GPIO4, LCD1.no_name_yet#15
  N2: Raspberry_Pi1.GND, Raspberry_Pi1.GPIO5, Raspberry_Pi1.GPIO13, Raspberry_Pi1.GPIO21
  N3: Raspberry_Pi1.GPIO17, LCD1.no_name_yet#16
  N4: Raspberry_Pi1.GPIO27, LCD1.no_name_yet#3
  N5: Raspberry_Pi1.GPIO22, LCD1.no_name_yet#5
  N6: Raspberry_Pi1.GPIO6, Raspberry_Pi1.GPIO12
  N7: Raspberry_Pi1.GPIO19, Raspberry_Pi1.GPIO16
  N8: Raspberry_Pi1.GPIO26, Raspberry_Pi1.GPIO20
  N9: Raspberry_Pi1.GPIO7, LCD1.no_name_yet#17
  N10: Raspberry_Pi1.GPIO25, LCD1.no_name_yet#10
  N11: Raspberry_Pi1.GPIO24, LCD1.no_name_yet#11
  N12: Raspberry_Pi1.GPIO23, LCD1.no_name_yet#12
  N13: Raspberry_Pi1.GPIO18, LCD1.no_name_yet#13
  N14: Raspberry_Pi1.5V, LCD1.no_name_yet#0, LCD1.no_name_yet#1, LCD1.no_name_yet#4, LCD1.no_name_yet#14, R1.CCW, R1.CW
  N15: LCD1.no_name_yet#2, R1.WIPER

custom parts:
  Adafruit Positive RGB 2x16 LCD: Adafruit Positive 2x16 LCD Display with RGB Backlight
