# Fritzing sketch rgb-lcd-rpi (saved by Fritzing 0.9.3b)
breadboards: 1

parts:
  Raspberry_Pi1 = Raspberry Pi 2
  LCD1 = Adafruit Positive RGB 2x16 LCD
  R1 = TRIMPOT [package=3386u]

nets:
  N1: Raspberry_Pi1.GPIO4, LCD1.no_name_yet#15
  N2: Raspberry_Pi1.GPIO17, LCD1.no_name_yet#16
  N3: Raspberry_Pi1.GPIO27, LCD1.no_name_yet#3
  N4: Raspberry_Pi1.GPIO22, LCD1.no_name_yet#5
  N5: Raspberry_Pi1.GPIO7, LCD1.no_name_yet#17
  N6: Raspberry_Pi1.GPIO25, LCD1.no_name_yet#10
  N7: Raspberry_Pi1.GPIO24, LCD1.no_name_yet#11
  N8: Raspberry_Pi1.GPIO23, LCD1.no_name_yet#12
  N9: Raspberry_Pi1.GPIO18, LCD1.no_name_yet#13
  N10: Raspberry_Pi1.5V, LCD1.no_name_yet#0, LCD1.no_name_yet#1, LCD1.no_name_yet#4, R1.CCW, R1.CW
  N11: LCD1.no_name_yet#2, R1.WIPER

custom parts:
  Adafruit Positive RGB 2x16 LCD: Adafruit Positive 2x16 LCD Display with RGB Backlight
